# Fritzing sketch Schematics (saved by Fritzing 0.7.12b)
breadboards: 1

parts:
  RaspberryPi1 = Raspberry Pi Model B
  R1 = Resistor [tolerance=±5% resistance=1 package=THT]
  R2 = Resistor [tolerance=±5% resistance=1 package=THT]
  R3 = Resistor [tolerance=±5% resistance=10 package=THT]
  R4 = Resistor [tolerance=±5% resistance=10 package=THT]
  S1 = Pushbutton [package="[THT]"]
  S2 = Pushbutton [package="[THT]"]

nets:
  N1: RaspberryPi1.3V3, S1.Pin_1, S1.Pin_2, S2.Pin_3, S2.Pin_4
  N2: RaspberryPi1.#17, R1.Pin_1
  N3: RaspberryPi1.#22, R2.Pin_0
  N4: R1.Pin_0, R4.Pin_1, S2.Pin_1, S2.Pin_2
  N5: R2.Pin_1, R3.Pin_0, S1.Pin_3, S1.Pin_4
  N6: R3.Pin_1, R4.Pin_0

custom parts:
  Raspberry Pi Model B: Raspberry Pi (Model B)
